# Fritzing sketch INFOMATRIX CXEMA 2026 (saved by Fritzing 0.9.5d)

parts:
  A1 = ESP32 devkit 38p expansion board
  BAT1 = 12 battery [package=battery]
  U1 = ESP32-38PinWide [part_number=ESP32-38PinWide]  # not connected
  A2 = motor driver ZK-5AD
  A3 = motor driver ZK-5AD
  J1 = Connector 2 In 4 out
  SW1 = Slide_Switch_new
  M1 = Getriebemotor
  M2 = Getriebemotor
  M3 = Getriebemotor
  M4 = Getriebemotor
  J2 = Connector 2 In 4 out
  JACK1 = 2.1mm Barrel Jack with Terminal Block

nets:
  N1: A1.Pin_8, A1.Pin_68, A3.Pin_6
  N2: A1.Pin_9, A1.Pin_88, A3.Pin_5
  N3: A1.Pin_11, A1.Pin_90, A3.Pin_4
  N4: A1.Pin_13, A1.Pin_93, A3.Pin_3
  N5: A1.Pin_50, A1.Pin_73, A1.Pin_144, A2.Pin_1, A3.Pin_1
  N6: A1.Pin_106, A1.Pin_167, A2.Pin_6
  N7: A1.Pin_107, A1.Pin_168, A2.Pin_5
  N8: A1.Pin_108, A1.Pin_169, A2.Pin_4
  N9: A1.Pin_109, A1.Pin_170, A2.Pin_3
  N10: BAT1.-, SW1.pin_2
  N11: BAT1.+, A3.Pin_12, J1.Pin_3, J1.Pin_5, J2.Pin_3, J2.Pin_4, J2.Pin_5, JACK1.NEG
  N12: A2.Pin_8, M3.pin_2
  N13: A2.Pin_9, M3.pin_1
  N14: A2.Pin_10, M1.pin_2
  N15: A2.Pin_11, M1.pin_1
  N16: A2.Pin_13, A3.Pin_13, J1.Pin_1, J1.Pin_2, J1.Pin_6, SW1.pin_1, J2.Pin_1, J2.Pin_2, J2.Pin_6, JACK1.POS
  N17: A3.Pin_8, M2.pin_2
  N18: A3.Pin_9, M2.pin_1
  N19: A3.Pin_10, M4.pin_2
  N20: A3.Pin_11, M4.pin_1

custom parts:
  ESP32 devkit 38p expansion board: Upgraded ESP32 38P Development ESP32-DevKitC-32 ESP-WROOM-32 Expansion Board.
  12 battery: 12V lead acid type battery, like the Husqvarna YTH2448 12V 35AH battery. This is the mini version 1/4 the size of the actual battery to be closer to typical breadboard parts (around 2in wide rathher than 7in). The pads in pcb are sized to accomidate up to 14ga wire (as these batterys will deliver high currents.)
  ESP32-38PinWide: Generic 38-Pin ESP32 with wide format (only access to one side of pins on a breadboard) based on Stephen Lilley's HiLetgo ESP-WROOM-32 ESP32 ESP-32S Development Board.
  motor driver ZK-5AD: 5A Dual Motor Drive Module Reverse PWM Speed Regulation Double H Bridge L298N Module DC 3.0V-14V.
  Slide_Switch_new: the New two pin slide switch
